# Fritzing sketch BME280_ESP8266 (saved by Fritzing 0.9.4)
breadboards: 1

parts:
  Componente1 = BME280 Breakout  # not connected
  U1 = NodeMCU V3.0

nets:
  N1: U1.D0, U1.RST
  N2: U1.GND#6, U1.GND#13, U1.GND#16, U1.GND#33

custom parts:
  NodeMCU V3.0: ESP8266 based NodeMCU
