# Fritzing sketch DS18B20_ESP8266 (saved by Fritzing 0.9.4)
breadboards: 1

parts:
  U1 = NodeMCU V3.0
  DS1 = DS18B20 1-Wire Temperature Sensor [part_number=DS18B20]
  R1 = Resistor [tolerance=±5% resistance=4.7k package="0402 [SMD]"]

nets:
  N1: U1.D0, U1.RST
  N2: U1.D4, DS1.DQ, R1.Pin_1
  3V3: U1.3V3, DS1.VDD, R1.Pin_0
  N3: U1.GND#6, U1.GND#13, U1.GND#16, U1.GND#33, DS1.GND

custom parts:
  NodeMCU V3.0: ESP8266 based NodeMCU
